# Fritzing sketch ohm_RGBLed-circuit (saved by Fritzing 0.9.2b)
circuit board: 7.5cm x 3.2cm
breadboards: 1

parts:
  Q1 = Basic FET N-Channel [package="TO220 [THT]"]
  Q2 = Basic FET N-Channel [package="TO220 [THT]"]
  Q3 = Basic FET N-Channel [package="TO220 [THT]"]
  J1 = Power Jack [package=power_jack_pth]
  RGB_LEDs = RGB Strip LED
  LED_connector = Header 4 [package=jst-4-pth]
  Part1 = HUZZAH ESP8266 Breakout
  U1 = Voltage Regulator - 5V [package="TO220 [THT]"]

nets:
  N1: Q1.gate, Part1.GPIO13
  N2: Q1.drain, RGB_LEDs.Blue_Connect, LED_connector.1
  GND: Q1.source, Q2.source, Q3.source, J1.GND, J1.GNDBREAK, Part1.GND, U1.GND
  N3: Q2.gate, Part1.GPIO12
  N4: Q2.drain, RGB_LEDs.Red_Connect, LED_connector.2
  N5: Q3.gate, Part1.GPIO14
  N6: Q3.drain, RGB_LEDs.Green_Connect, LED_connector.3
  N7: J1.PWR, RGB_LEDs.Common_Connect, LED_connector.4, U1.input_voltage
  N8: Part1.VIN, U1.output_voltage

custom parts:
  RGB Strip LED: A tri-color Strip LED with red, green and blue. Based on LED SMD 5050 RGB Pin order: common cathode - green - red - blue
  HUZZAH ESP8266 Breakout: The ESP8266 processor from Espressif is an 80 MHz microcontroller with a full WiFi front-end (both as client and access point) and TCP/IP stack with DNS support as well.
