# Fritzing sketch stripboard version (saved by Fritzing 0.9.2b)
stripboards: 1

parts:
  Part1 = HUZZAH ESP8266 Breakout
  Power_plug1 = Power plug
  JP2 = Header 4 [package=molex-1x4_lock]
  Q1 = Basic FET N-Channel [package="TO220 [THT]"]
  Q2 = Basic FET N-Channel [package="TO220 [THT]"]
  Q3 = Basic FET N-Channel [package="TO220 [THT]"]

nets:
  N1: Part1.GPIO14, Q3.source
  N2: Part1.GPIO12, Q1.source
  N3: Part1.GPIO13, Q2.source
  GND: Part1.GND, Power_plug1.GND, Q1.gate, Q2.gate, Q3.gate
  N4: JP2.2, Q3.drain
  N5: JP2.3, Q1.drain
  N6: JP2.4, Q2.drain

custom parts:
  HUZZAH ESP8266 Breakout: The ESP8266 processor from Espressif is an 80 MHz microcontroller with a full WiFi front-end (both as client and access point) and TCP/IP stack with DNS support as well.
